// Logisim project MINI_MIPS_ALU_Control.circ as structural Verilog: 1 circuit, main circuit main
module main (
  input  ALUop1,
  input  ALUop0,
  input  F2,
  input  F1,
  input  F0,
  output Ainv,
  output Bneg,
  output Op1,
  output Op0
);

  wire and_1_out, and_2_out, and_3_out, and_4_out, and_5_out, and_6_out, and_7_out, and_8_out, and_9_out,
       and_11_out, or_1_out, or_2_out, xnor_1_out;

  and and_1 (and_1_out, ~ALUop1, ALUop0);  // AND_Gate
  and and_2 (and_2_out, ALUop1, ~ALUop0);  // AND_Gate
  and and_3 (and_3_out, F1, F0);
  and and_4 (and_4_out, ~F2, F0);  // AND_Gate
  and and_5 (and_5_out, ~F2, F1);  // AND_Gate
  and and_6 (and_6_out, ~F2, ~F0);  // AND_Gate
  and and_7 (and_7_out, ~F1, F0);  // AND_Gate
  and and_8 (and_8_out, ~F2, F1, ~F0);  // AND_Gate
  and and_9 (and_9_out, ALUop1, ~ALUop0, F0);  // AND_Gate
  and and_10 (Ainv, and_9_out, xnor_1_out);
  xnor xnor_1 (xnor_1_out, F2, F1);
  or or_1 (or_1_out, and_3_out, and_4_out, and_5_out);
  or or_2 (or_2_out, and_7_out, and_8_out);
  and and_11 (and_11_out, and_2_out, or_1_out);
  or or_3 (Op1, and_5_out, and_6_out, ~ALUop1, ALUop0);  // OR_Gate
  and and_12 (Op0, and_2_out, or_2_out);
  or or_4 (Bneg, and_1_out, and_11_out);
endmodule
