// Logisim project ULA_1_BIT_Mini_Mips_15.circ as structural Verilog: 1 circuit, main circuit main
module main (
  input  AInv,
  input  BInv,
  input  CIn,
  input  ALUOp1,
  input  ALUOp0,
  input  A,
  input  B,
  input  Less,
  output Result,
  output Set,
  output Overflow,
  output COut
);

  wire and_1_out, and_2_out, and_3_out, multiplexer_1_out, multiplexer_2_out, not_1_out, not_2_out, or_1_out,
       xor_1_out;

  not not_1 (not_1_out, A);
  not not_2 (not_2_out, B);
  Multiplexer #(.disabled(0), .enable("false")) multiplexer_1 (
    .in0(A), .in1(not_1_out), .out(multiplexer_1_out), .sel(AInv));
  Multiplexer #(.disabled(0), .enable("false")) multiplexer_2 (
    .in0(B), .in1(not_2_out), .out(multiplexer_2_out), .sel(BInv));
  and and_1 (and_1_out, multiplexer_1_out, multiplexer_2_out);
  or or_1 (or_1_out, multiplexer_1_out, multiplexer_2_out);
  and and_2 (and_2_out, multiplexer_1_out, multiplexer_2_out);
  xor xor_1 (xor_1_out, multiplexer_1_out, multiplexer_2_out);
  or or_2 (COut, and_2_out, and_3_out);
  and and_3 (and_3_out, xor_1_out, CIn);
  xor xor_2 (Set, CIn, xor_1_out);
  Multiplexer #(.select(2), .disabled(0), .enable("false")) multiplexer_3 (
    .in0(and_1_out), .in1(or_1_out), .in2(Set), .in3(Less), .out(Result), .sel({ALUOp1, ALUOp0}));
  xor xor_3 (Overflow, CIn, COut);
endmodule
