// Logisim project DataMemory_16bits.circ as structural Verilog: 1 circuit, main circuit main
module main (
  input  [15:0] Address,
  input  [15:0] WriteData,
  input  MemWrite,
  input  MemRead,
  input  Clock,
  output [15:0] ReadData
);

  wire or_1_out;
  wire [15:0] shifter_1_out;

  Shifter #(.width(16), .shift("lr")) shifter_1 (.in(Address), .\dist (4'b0001), .out(shifter_1_out));
  or or_1 (or_1_out, MemWrite, MemRead);
  RAM #(.addrWidth(16), .dataWidth(16), .bus("separate")) ram_1 (
    .addr(shifter_1_out), .din(WriteData), .data(ReadData), .str(MemWrite), .sel(or_1_out), .clk(Clock),
    .ld(MemRead));  // open: clr
endmodule
