// Logisim project ULA_16_BITS.circ as structural Verilog: 1 circuit, main circuit main
module main (
  input  AInv,
  input  BInv,
  input  ALUOp1,
  input  ALUOp0,
  input  [15:0] A,
  input  [15:0] B,
  output ZERO_COMP,
  output [15:0] Result,
  output Overflow
);

  wire main_1_cout, main_2_cout, main_3_cout, main_4_cout, main_5_cout, main_6_cout, main_7_cout,
       main_8_cout, main_9_cout, main_10_cout, main_11_cout, main_12_cout, main_13_cout, main_14_cout,
       main_15_cout, main_16_set;

  ULA_1_BIT_Mini_Mips_0_14_main main_1 (
    .A(A[0]), .B(B[0]), .Less(main_16_set), .AInv(AInv), .BInv(BInv), .CIn(BInv), .ALUOp1(ALUOp1),
    .ALUOp0(ALUOp0), .COut(main_1_cout), .Result(Result[0]));
  ULA_1_BIT_Mini_Mips_0_14_main main_2 (
    .A(A[1]), .B(B[1]), .Less(1'b0), .AInv(AInv), .BInv(BInv), .CIn(main_1_cout), .ALUOp1(ALUOp1),
    .ALUOp0(ALUOp0), .COut(main_2_cout), .Result(Result[1]));
  ULA_1_BIT_Mini_Mips_0_14_main main_3 (
    .A(A[2]), .B(B[2]), .Less(1'b0), .AInv(AInv), .BInv(BInv), .CIn(main_2_cout), .ALUOp1(ALUOp1),
    .ALUOp0(ALUOp0), .COut(main_3_cout), .Result(Result[2]));
  ULA_1_BIT_Mini_Mips_0_14_main main_4 (
    .A(A[3]), .B(B[3]), .Less(1'b0), .AInv(AInv), .BInv(BInv), .CIn(main_3_cout), .ALUOp1(ALUOp1),
    .ALUOp0(ALUOp0), .COut(main_4_cout), .Result(Result[3]));
  ULA_1_BIT_Mini_Mips_0_14_main main_5 (
    .A(A[4]), .B(B[4]), .Less(1'b0), .AInv(AInv), .BInv(BInv), .CIn(main_4_cout), .ALUOp1(ALUOp1),
    .ALUOp0(ALUOp0), .COut(main_5_cout), .Result(Result[4]));
  ULA_1_BIT_Mini_Mips_0_14_main main_6 (
    .A(A[5]), .B(B[5]), .Less(1'b0), .AInv(AInv), .BInv(BInv), .CIn(main_5_cout), .ALUOp1(ALUOp1),
    .ALUOp0(ALUOp0), .COut(main_6_cout), .Result(Result[5]));
  ULA_1_BIT_Mini_Mips_0_14_main main_7 (
    .A(A[6]), .B(B[6]), .Less(1'b0), .AInv(AInv), .BInv(BInv), .CIn(main_6_cout), .ALUOp1(ALUOp1),
    .ALUOp0(ALUOp0), .COut(main_7_cout), .Result(Result[6]));
  ULA_1_BIT_Mini_Mips_0_14_main main_8 (
    .A(A[7]), .B(B[7]), .Less(1'b0), .AInv(AInv), .BInv(BInv), .CIn(main_7_cout), .ALUOp1(ALUOp1),
    .ALUOp0(ALUOp0), .COut(main_8_cout), .Result(Result[7]));
  ULA_1_BIT_Mini_Mips_0_14_main main_9 (
    .A(A[8]), .B(B[8]), .Less(1'b0), .AInv(AInv), .BInv(BInv), .CIn(main_8_cout), .ALUOp1(ALUOp1),
    .ALUOp0(ALUOp0), .COut(main_9_cout), .Result(Result[8]));
  ULA_1_BIT_Mini_Mips_0_14_main main_10 (
    .A(A[9]), .B(B[9]), .Less(1'b0), .AInv(AInv), .BInv(BInv), .CIn(main_9_cout), .ALUOp1(ALUOp1),
    .ALUOp0(ALUOp0), .COut(main_10_cout), .Result(Result[9]));
  ULA_1_BIT_Mini_Mips_0_14_main main_11 (
    .A(A[10]), .B(B[10]), .Less(1'b0), .AInv(AInv), .BInv(BInv), .CIn(main_10_cout), .ALUOp1(ALUOp1),
    .ALUOp0(ALUOp0), .COut(main_11_cout), .Result(Result[10]));
  ULA_1_BIT_Mini_Mips_0_14_main main_12 (
    .A(A[11]), .B(B[11]), .Less(1'b0), .AInv(AInv), .BInv(BInv), .CIn(main_11_cout), .ALUOp1(ALUOp1),
    .ALUOp0(ALUOp0), .COut(main_12_cout), .Result(Result[11]));
  ULA_1_BIT_Mini_Mips_0_14_main main_13 (
    .A(A[12]), .B(B[12]), .Less(1'b0), .AInv(AInv), .BInv(BInv), .CIn(main_12_cout), .ALUOp1(ALUOp1),
    .ALUOp0(ALUOp0), .COut(main_13_cout), .Result(Result[12]));
  ULA_1_BIT_Mini_Mips_0_14_main main_14 (
    .A(A[13]), .B(B[13]), .Less(1'b0), .AInv(AInv), .BInv(BInv), .CIn(main_13_cout), .ALUOp1(ALUOp1),
    .ALUOp0(ALUOp0), .COut(main_14_cout), .Result(Result[13]));
  ULA_1_BIT_Mini_Mips_0_14_main main_15 (
    .A(A[14]), .B(B[14]), .Less(1'b0), .AInv(AInv), .BInv(BInv), .CIn(main_14_cout), .ALUOp1(ALUOp1),
    .ALUOp0(ALUOp0), .COut(main_15_cout), .Result(Result[14]));
  ULA_1_BIT_Mini_Mips_15_main main_16 (
    .A(A[15]), .B(B[15]), .Less(1'b0), .AInv(AInv), .BInv(BInv), .CIn(main_15_cout), .ALUOp1(ALUOp1),
    .ALUOp0(ALUOp0), .Result(Result[15]), .Set(main_16_set), .Overflow(Overflow));  // open: COut
  nor nor_1 (ZERO_COMP, Result[0], Result[1], Result[2], Result[3], Result[4], Result[5], Result[6], Result[7], Result[8], Result[9], Result[10], Result[11], Result[12], Result[13], Result[14], Result[15]);

  // Notes on the sheet:
  //   ULA
endmodule
