// Logisim project decoder_example.circ as structural Verilog: 1 circuit, main circuit main
module main (
  input  [7:0] in_1,
  input  in_2,
  input  in_3
);

  wire and_1_out, and_2_out, and_3_out, and_4_out, clock_1_out, clock_2_out, controlled_buffer_1_out,
       not_1_out;
  wire [7:0] counter_1_q;

  and and_1 (and_1_out, ~in_2, ~in_3);  // AND_Gate
  and and_2 (and_2_out, ~in_2, in_3);  // AND_Gate
  assign controlled_buffer_1_out = and_2_out ? 1'b1 : 1'bz;  // Controlled_Buffer controlled_buffer_1
  and and_3 (and_3_out, in_2, ~in_3);  // AND_Gate
  Random #(.width(2)) random_1 (.clk(clock_2_out), .next(and_4_out));  // open: out, clr
  and and_4 (and_4_out, in_2, in_3);
  Counter counter_1 (.count(and_1_out), .Q(counter_1_q), .clk(clock_1_out));  // open: load, D, carry, clr
  Clock clock_1 (.out(clock_1_out));
  LED led_1 (.in(controlled_buffer_1_out));
  not not_1 (not_1_out, and_3_out);
  Shift_Register shift_register_1 (
    .shift(and_3_out), .in(1'b0), .clk(clock_2_out), .load(not_1_out), .d0(in_1[7]), .d1(in_1[6]),
    .d2(in_1[5]), .d3(in_1[4]), .d4(in_1[3]), .d5(in_1[2]), .d6(in_1[1]), .d7(in_1[0]));  // open: out, clr, q0, q1, q2, q3, q4, q5, q6, q7
  Clock clock_2 (.out(clock_2_out));
  DotMatrix #(.matrixcols(8), .matrixrows(1)) dotmatrix_1 (
    .col0(counter_1_q[7]), .col1(counter_1_q[6]), .col2(counter_1_q[5]), .col3(counter_1_q[4]),
    .col4(counter_1_q[3]), .col5(counter_1_q[2]), .col6(counter_1_q[1]), .col7(counter_1_q[0]));
endmodule
