// Logisim project MINI_MIPS_Control.circ as structural Verilog: 1 circuit, main circuit main
module main (
  input  OpCode3,
  input  OpCode2,
  input  OpCode1,
  input  OpCode0,
  output RegDst,
  output Jump,
  output Branch,
  output MemRead,
  output MemtoReg,
  output ALUop1,
  output ALUop0,
  output MemWrite,
  output ALUsrc,
  output RegWrite
);

  wire and_7_out, and_9_out;

  and and_1 (RegDst, ~OpCode3, ~OpCode1, ~OpCode0);  // AND_Gate
  and and_2 (Jump, ~OpCode3, ~OpCode2, OpCode1, ~OpCode0);  // AND_Gate
  and and_3 (Branch, ~OpCode3, OpCode2, ~OpCode1, ~OpCode0);  // AND_Gate
  and and_4 (MemRead, ~OpCode3, ~OpCode2, OpCode1, OpCode0);  // AND_Gate
  and and_5 (MemtoReg, ~OpCode3, ~OpCode2, OpCode1);  // AND_Gate
  and and_6 (ALUop1, ~OpCode2, ~OpCode1, ~OpCode0);  // AND_Gate
  and and_7 (and_7_out, OpCode3, ~OpCode2, ~OpCode1, ~OpCode0);  // AND_Gate
  and and_8 (MemWrite, OpCode3, ~OpCode2, OpCode1, ~OpCode0);  // AND_Gate
  and and_9 (and_9_out, OpCode3, ~OpCode2, ~OpCode0);  // AND_Gate
  or or_1 (ALUop0, Branch, and_7_out);
  or or_2 (ALUsrc, MemtoReg, and_9_out);
  or or_3 (RegWrite, ALUop1, MemRead);
endmodule
