// Logisim project MINI_MIPS_16_Bits.circ as structural Verilog: 1 circuit, main circuit main
module main (
  input  ClearPC,
  output [15:0] PC_2,
  output [11:0] Adrress,
  output [15:0] PC_2_BranchAddr,
  output [3:0] OpCode,
  output [15:0] JumpAddr,
  output [15:0] BranchAdrr,
  output [15:0] PC,
  output [15:0] NewPC,
  output [15:0] Instruction_Bits,
  output [15:0] Read_Data_1,
  output [15:0] ALU_Out,
  output [2:0] rs,
  output [15:0] Write_Data,
  output [2:0] rt,
  output [2:0] rd,
  output [15:0] Imm_16,
  output [2:0] funct,
  output [15:0] Read_Data_2
);

  wire ALUop0, ALUop1, ALUsrc, and_1_out, Branch, Clock_out, Jump, main_4_ainv, main_4_bneg, main_4_op0,
       main_4_op1, main_5_overflow, main_5_zero_comp, MemRead, MemtoReg, MemWrite, RegDst, RegWrite;
  wire [2:0] multiplexer_1_out;
  wire [12:0] bit_extender_1_out;
  wire [15:0] main_6_readdata, multiplexer_2_out, multiplexer_3_out;

  Register #(.width(16)) u_PC (.D(NewPC), .en(1'b1), .Q(PC), .clk(Clock_out), .clr(ClearPC));
  Clock Clock (.out(Clock_out));
  Adder #(.width(16)) adder_1 (.a(PC), .b(16'h2), .out({JumpAddr[15:13], PC_2[12:0]}));  // open: cin, cout
  DataMemory_16bits_main main_1 (
    .MemWrite(1'b0), .MemRead(1'b1), .ReadData({Instruction_Bits[15:12], Adrress}), .Address(PC),
    .Clock(Clock_out));  // open: WriteData
  assign bit_extender_1_out = {{1{1'b0}}, Adrress};  // Bit_Extender bit_extender_1
  MINI_MIPS_Control_main main_2 (
    .OpCode3(Instruction_Bits[15]), .OpCode2(Instruction_Bits[14]), .OpCode1(Instruction_Bits[13]),
    .OpCode0(Instruction_Bits[12]), .RegDst(RegDst), .Jump(Jump), .Branch(Branch), .MemRead(MemRead),
    .MemtoReg(MemtoReg), .ALUop1(ALUop1), .ALUop0(ALUop0), .MemWrite(MemWrite), .ALUsrc(ALUsrc),
    .RegWrite(RegWrite));
  Multiplexer #(.width(3), .enable("false")) multiplexer_1 (
    .in0(Adrress[8:6]), .in1(Adrress[5:3]), .out(multiplexer_1_out), .sel(RegDst));
  assign Imm_16 = {{10{Adrress[5]}}, Adrress[5:0]};  // Bit_Extender bit_extender_2
  Shifter #(.width(13)) shifter_1 (.in(bit_extender_1_out), .\dist (4'b0001), .out(JumpAddr[12:0]));
  Registers_bank_16_bits_main main_3 (
    .Read_Ragister_1(Adrress[11:9]), .Read_Register_2(Adrress[8:6]), .Write_Register(multiplexer_1_out),
    .Write_Data(Write_Data), .RegWrite(RegWrite), .Clock(Clock_out), .Read_Data_1(Read_Data_1),
    .Read_Data_2(Read_Data_2));
  Shifter #(.width(16)) shifter_2 (.in(Imm_16), .\dist (4'b0001), .out(BranchAdrr));
  Multiplexer #(.width(16), .enable("false")) multiplexer_2 (
    .in0(Read_Data_2), .in1(Imm_16), .out(multiplexer_2_out), .sel(ALUsrc));
  MINI_MIPS_ALU_Control_main main_4 (
    .ALUop1(ALUop1), .ALUop0(ALUop0), .F2(Adrress[2]), .F1(Adrress[1]), .F0(Adrress[0]), .Ainv(main_4_ainv),
    .Bneg(main_4_bneg), .Op1(main_4_op1), .Op0(main_4_op0));
  Adder #(.width(16)) adder_2 (
    .a({JumpAddr[15:13], PC_2[12:0]}), .b(BranchAdrr), .out(PC_2_BranchAddr));  // open: cin, cout
  ULA_16_BITS_main main_5 (
    .A(Read_Data_1), .B(multiplexer_2_out), .ZERO_COMP(main_5_zero_comp), .Result(ALU_Out),
    .Overflow(main_5_overflow), .AInv(main_4_ainv), .BInv(main_4_bneg), .ALUOp1(main_4_op1),
    .ALUOp0(main_4_op0));
  LED Overflow (.in(main_5_overflow));
  Multiplexer #(.width(16), .enable("false")) multiplexer_3 (
    .in0({JumpAddr[15:13], PC_2[12:0]}), .in1(PC_2_BranchAddr), .out(multiplexer_3_out), .sel(and_1_out));
  and and_1 (and_1_out, Branch, main_5_zero_comp);
  LED indica_resultado_igual_a__zero_na_ALU (.in(main_5_zero_comp));
  DataMemory_16bits_main main_6 (
    .WriteData(Read_Data_2), .MemWrite(MemWrite), .MemRead(MemRead), .ReadData(main_6_readdata),
    .Address(ALU_Out), .Clock(Clock_out));
  Multiplexer #(.width(16), .enable("false")) multiplexer_4 (
    .in0(multiplexer_3_out), .in1(JumpAddr), .out(NewPC), .sel(Jump));
  Multiplexer #(.width(16), .enable("false")) multiplexer_5 (
    .in0(ALU_Out), .in1(main_6_readdata), .out(Write_Data), .sel(MemtoReg));

  assign funct = Adrress[2:0];
  assign Instruction_Bits[11:0] = Adrress;
  assign OpCode = Instruction_Bits[15:12];
  assign PC_2[15:13] = JumpAddr[15:13];
  assign rd = Adrress[5:3];
  assign rs = Adrress[11:9];
  assign rt = Adrress[8:6];

  // Notes on the sheet:
  //   MINI MIPS 16bits
endmodule
