// Logisim project DataMemory.circ as structural Verilog: 1 circuit, main circuit main
module main (
  input  [7:0] in_1,
  input  [7:0] in_2,
  input  MemWrite,
  input  MemRead
);

  wire clock_1_out, or_1_out;
  wire [7:0] ram_1_data;

  Clock clock_1 (.out(clock_1_out));
  or or_1 (or_1_out, MemWrite, MemRead);
  RAM #(.bus("separate")) ram_1 (
    .addr(in_1), .din(in_2), .data(ram_1_data), .str(MemWrite), .sel(or_1_out), .clk(clock_1_out),
    .ld(MemRead));  // open: clr
  DotMatrix #(.matrixcols(8), .matrixrows(1)) dotmatrix_1 (
    .col0(ram_1_data[7]), .col1(ram_1_data[6]), .col2(ram_1_data[5]), .col3(ram_1_data[4]),
    .col4(ram_1_data[3]), .col5(ram_1_data[2]), .col6(ram_1_data[1]), .col7(ram_1_data[0]));

  // Notes on the sheet:
  //   WriteData
  //   Address
  //   ReadData
endmodule
