// Logisim project Registers_bank.circ as structural Verilog: 1 circuit, main circuit main
module main (
  input  [1:0] Read_Register_1,
  input  [1:0] Read_Register_2,
  input  [1:0] Write_Register,
  input  [7:0] in_4,
  input  RegWrite
);

  wire clock_1_out, decoder_1_out0, decoder_1_out1, decoder_1_out2, decoder_1_out3;
  wire [7:0] multiplexer_1_out, multiplexer_2_out, register_1_q, register_2_q, register_3_q, register_4_q;

  Clock clock_1 (.out(clock_1_out));
  Decoder #(.select(2), .disabled(0)) decoder_1 (
    .out0(decoder_1_out0), .out1(decoder_1_out1), .out2(decoder_1_out2), .out3(decoder_1_out3),
    .sel(Write_Register), .en(RegWrite));
  Register register_1 (.D(in_4), .en(decoder_1_out0), .Q(register_1_q), .clk(clock_1_out));  // open: clr
  Register register_2 (.D(in_4), .en(decoder_1_out1), .Q(register_2_q), .clk(clock_1_out));  // open: clr
  Register register_3 (.D(in_4), .en(decoder_1_out2), .Q(register_3_q), .clk(clock_1_out));  // open: clr
  Register register_4 (.D(in_4), .en(decoder_1_out3), .Q(register_4_q), .clk(clock_1_out));  // open: clr
  Multiplexer #(.select(2), .width(8)) multiplexer_1 (
    .in0(register_1_q), .in1(register_2_q), .in2(register_3_q), .in3(register_4_q), .out(multiplexer_1_out),
    .sel(Read_Register_1), .en(1'b1));
  Multiplexer #(.select(2), .width(8)) multiplexer_2 (
    .in0(register_1_q), .in1(register_2_q), .in2(register_3_q), .in3(register_4_q), .out(multiplexer_2_out),
    .sel(Read_Register_2), .en(1'b1));
  DotMatrix #(.matrixcols(8), .matrixrows(1)) dotmatrix_1 (
    .col0(multiplexer_1_out[7]), .col1(multiplexer_1_out[6]), .col2(multiplexer_1_out[5]),
    .col3(multiplexer_1_out[4]), .col4(multiplexer_1_out[3]), .col5(multiplexer_1_out[2]),
    .col6(multiplexer_1_out[1]), .col7(multiplexer_1_out[0]));
  DotMatrix #(.matrixcols(8), .matrixrows(1)) dotmatrix_2 (
    .col0(multiplexer_2_out[7]), .col1(multiplexer_2_out[6]), .col2(multiplexer_2_out[5]),
    .col3(multiplexer_2_out[4]), .col4(multiplexer_2_out[3]), .col5(multiplexer_2_out[2]),
    .col6(multiplexer_2_out[1]), .col7(multiplexer_2_out[0]));

  // Notes on the sheet:
  //   Write Data
  //   Clock
endmodule
