// Logisim project SignExtender.circ as structural Verilog: 1 circuit, main circuit main
module main (
  input  [7:0] in_1
);

  wire [15:0] bit_extender_1_out;

  DotMatrix #(.matrixcols(16), .matrixrows(1)) dotmatrix_1 (
    .col0(bit_extender_1_out[15]), .col1(bit_extender_1_out[14]), .col2(bit_extender_1_out[13]),
    .col3(bit_extender_1_out[12]), .col4(bit_extender_1_out[11]), .col5(bit_extender_1_out[10]),
    .col6(bit_extender_1_out[9]), .col7(bit_extender_1_out[8]), .col8(bit_extender_1_out[7]),
    .col9(bit_extender_1_out[6]), .col10(bit_extender_1_out[5]), .col11(bit_extender_1_out[4]),
    .col12(bit_extender_1_out[3]), .col13(bit_extender_1_out[2]), .col14(bit_extender_1_out[1]),
    .col15(bit_extender_1_out[0]));
  assign bit_extender_1_out = {{8{in_1[7]}}, in_1};  // Bit_Extender bit_extender_1
endmodule
