// Logisim project register_example.circ as structural Verilog: 1 circuit, main circuit main
module main (
  input  [7:0] Input,
  input  Enable
);

  wire clock_1_out;
  wire [7:0] register_1_q;

  Register register_1 (.D(Input), .en(Enable), .Q(register_1_q), .clk(clock_1_out));  // open: clr
  Clock clock_1 (.out(clock_1_out));
  DotMatrix #(.matrixcols(8), .matrixrows(1)) dotmatrix_1 (
    .col0(register_1_q[7]), .col1(register_1_q[6]), .col2(register_1_q[5]), .col3(register_1_q[4]),
    .col4(register_1_q[3]), .col5(register_1_q[2]), .col6(register_1_q[1]), .col7(register_1_q[0]));

  // Notes on the sheet:
  //   Clock
  //   Output
endmodule
